# Fritzing sketch battery (saved by Fritzing 0.9.4)
circuit board: 4.3561cm x 4.98493cm
breadboards: 1

parts:
  Part3 = Arduino Nano 33 BLE Sense
  J2 = screw terminal, 2 pins
  R4 = Resistor [tolerance=±5% resistance=100k package=THT]
  Q2 = TRANSISTOR_NPN [package=to-92-ammo]
  J3 = screw terminal, 2 pins
  J4 = screw terminal, 2 pins

nets:
  N1: Part3.RX, J4.pin2
  N2: Part3.GND, J2.pin2, J4.pin1
  N3: Part3.D2, R4.Pin_1
  N4: Part3.VIN, J2.pin1
  N5: R4.Pin_0, Q2.B
  N6: Q2.E, J3.pin2
  N7: Q2.C, J3.pin1

notes:
  +
  -
  I1
  I2
  RX

custom parts:
  Arduino Nano 33 BLE Sense: The Nano 33 BLE Sense (without headers) is Arduino’s 3.3V AI enabled board in the smallest available form factor: 45x18mm! The Arduino Nano 33 BLE Sense is a completely new board on a well-known form factor. It comes with a series of embedded sensors: 9 axis inertial sensor: what makes this board ideal for wearable devices humidity, and temperature sensor: to get highly accurate measurements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
