# Fritzing sketch gps (saved by Fritzing 0.9.4)
circuit board: 5.25071cm x 5.63762cm
breadboards: 1

parts:
  Part1 = Arduino Nano 33 BLE Sense
  J2 = screw terminal, 2 pins
  Part2 = Adafruit Ultimate GPS v3 [part_number="Adafruit #746"]

nets:
  N1: Part1.TX, Part2.RX
  N2: Part1.RX, Part2.TX
  GND: Part1.GND, J2.pin2, Part2.GND
  N3: Part1.D2, Part2.FIX
  VIN: Part1.VIN, J2.pin1, Part2.VIN

notes:
  Dave Flanagan 2020
  +
  -

custom parts:
  Arduino Nano 33 BLE Sense: The Nano 33 BLE Sense (without headers) is Arduino’s 3.3V AI enabled board in the smallest available form factor: 45x18mm! The Arduino Nano 33 BLE Sense is a completely new board on a well-known form factor. It comes with a series of embedded sensors: 9 axis inertial sensor: what makes this board ideal for wearable devices humidity, and temperature sensor: to get highly accurate measurements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
  Adafruit Ultimate GPS v3: We carry a few different GPS modules here in the Adafruit shop, but none that satisfied our every desire - that's why we designed this little GPS breakout board. We believe this is the Ultimate GPS module, so we named it that. It's got everything you want and more: -165 dBm sensitivity, 10 Hz updates, 66 channels 5V friendly design and only 20mA current draw Breadboard friendly + two mounting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
