# Fritzing sketch heater (saved by Fritzing 0.9.4)
circuit board: 6.59632cm x 4.66703cm
breadboards: 1

parts:
  Part3 = Arduino Nano 33 BLE Sense
  J2 = screw terminal, 2 pins
  J3 = screw terminal, 3 pins
  Part4 = Logic Level Converter
  Q1 = TRANSISTOR_NPN [package=to-92-ammo]
  Q2 = PNP-Transistor [package="TO92 [THT]"]
  R1 = Resistor [tolerance=±5% resistance=100k package=THT]
  R2 = Resistor [tolerance=±5% resistance=100k package=THT]

nets:
  N1: Part3.TX, Part4.TX_LV
  N2: Part3.RX, Part4.RX_LV
  GND: Part3.GND, J2.pin2, J3.pin3, Part4.GND
  N3: Part3.D2, R1.Pin_0, R2.Pin_0
  N4: Part3.VIN, J2.pin1
  N5: Part3.3V3, Part4.LV
  N6: J3.pin1, Part4.HV
  N7: J3.pin2, Q1.C, Q2.E
  N8: Part4.TX_HV, Q1.E
  N9: Part4.RX_HV, Q2.C
  N10: Q1.B, R1.Pin_1
  N11: Q2.B, R2.Pin_1

notes:
  Dave Flanagan 2020
  -
  +
  D

custom parts:
  Arduino Nano 33 BLE Sense: The Nano 33 BLE Sense (without headers) is Arduino’s 3.3V AI enabled board in the smallest available form factor: 45x18mm! The Arduino Nano 33 BLE Sense is a completely new board on a well-known form factor. It comes with a series of embedded sensors: 9 axis inertial sensor: what makes this board ideal for wearable devices humidity, and temperature sensor: to get highly accurate measurements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
