# Fritzing sketch light (saved by Fritzing 0.9.4)
circuit board: 5.29505cm x 5cm
breadboards: 1

parts:
  Part2 = Arduino Nano 33 BLE Sense
  J1 = screw terminal, 2 pins
  J2 = screw terminal, 2 pins
  J3 = screw terminal, 2 pins
  J4 = screw terminal, 2 pins
  Q3 = Basic FET N-Channel [package="TO220 [THT]"]
  Q2 = Basic FET N-Channel [package="TO220 [THT]"]
  Q1 = Basic FET N-Channel [package="TO220 [THT]"]
  R1 = Resistor [tolerance=±5% resistance=10k package=THT]
  R2 = Resistor [tolerance=±5% resistance=10k package=THT]
  R3 = Resistor [tolerance=±5% resistance=10k package=THT]

nets:
  N1: Part2.GND, Part2.A7, J1.pin2, Q3.source, Q2.source, Q1.source, R1.Pin_1, R2.Pin_1, R3.Pin_1
  N2: Part2.VIN, J1.pin1, J2.pin1, J3.pin1, J4.pin1
  N3: Part2.A2, Q3.gate, R1.Pin_0
  N4: Part2.A1, Q2.gate, R2.Pin_0
  N5: Part2.A0, Q1.gate, R3.Pin_0
  N6: J2.pin2, Q1.drain
  N7: J3.pin2, Q2.drain
  N8: J4.pin2, Q3.drain

notes:
  Dave Flanagan 2020
  +
  -

custom parts:
  Arduino Nano 33 BLE Sense: The Nano 33 BLE Sense (without headers) is Arduino’s 3.3V AI enabled board in the smallest available form factor: 45x18mm! The Arduino Nano 33 BLE Sense is a completely new board on a well-known form factor. It comes with a series of embedded sensors: 9 axis inertial sensor: what makes this board ideal for wearable devices humidity, and temperature sensor: to get highly accurate measurements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
