# Fritzing sketch power (saved by Fritzing 0.9.4)
circuit board: 5cm x 11cm
breadboards: 1

parts:
  J3 = screw terminal, 2 pins
  J4 = screw terminal, 2 pins
  J5 = screw terminal, 2 pins
  J6 = screw terminal, 2 pins
  J7 = screw terminal, 2 pins
  J8 = screw terminal, 2 pins
  J9 = screw terminal, 2 pins
  J10 = screw terminal, 2 pins
  S1 = SPST Switch [package=switch-spdt_kit]
  S2 = SPST Switch [package=switch-spdt_kit]
  S3 = SPST Switch [package=switch-spdt_kit]
  S4 = SPST Switch [package=switch-spdt_kit]
  S5 = SPST Switch [package=switch-spdt_kit]
  S6 = SPST Switch [package=switch-spdt_kit]
  S7 = SPST Switch [package=switch-spdt_kit]
  R4 = Resistor [tolerance=±5% resistance=1k package=THT]
  R5 = Resistor [tolerance=±5% resistance=1k package=THT]
  R6 = Resistor [tolerance=±5% resistance=1k package=THT]
  R7 = Resistor [tolerance=±5% resistance=1k package=THT]
  R8 = Resistor [tolerance=±5% resistance=1k package=THT]
  R9 = Resistor [tolerance=±5% resistance=1k package=THT]
  R10 = Resistor [tolerance=±5% resistance=1k package=THT]
  LED5 = LED - 3mm [color="Red (633nm)" package="3 mm [THT]"]
  LED6 = LED - 3mm [color="Red (633nm)" package="3 mm [THT]"]
  LED4 = LED - 3mm [color="Red (633nm)" package="3 mm [THT]"]
  LED7 = LED - 3mm [color="Red (633nm)" package="3 mm [THT]"]
  LED8 = LED - 3mm [color="Red (633nm)" package="3 mm [THT]"]
  LED9 = LED - 3mm [color="Red (633nm)" package="3 mm [THT]"]
  LED10 = LED - 3mm [color="Red (633nm)" package="3 mm [THT]"]

nets:
  N1: J3.pin1, S1.P, S2.P, S3.P, S4.P, S5.P, S6.P, S7.P
  GND: J3.pin2, J4.pin2, J5.pin2, J6.pin2, J7.pin2, J8.pin2, J9.pin2, J10.pin2, LED5.cathode, LED6.cathode, LED4.cathode, LED7.cathode, LED8.cathode, LED9.cathode, LED10.cathode
  N2: J4.pin1, S1.O, R4.Pin_0
  N3: J5.pin1, S2.O, R5.Pin_0
  N4: J6.pin1, S3.O, R6.Pin_0
  N5: J7.pin1, S4.O, R7.Pin_0
  N6: J8.pin1, S5.O, R8.Pin_0
  N7: J9.pin1, S6.O, R9.Pin_0
  N8: J10.pin1, S7.O, R10.Pin_0
  N9: R4.Pin_1, LED4.anode
  N10: R5.Pin_1, LED5.anode
  N11: R6.Pin_1, LED6.anode
  N12: R7.Pin_1, LED7.anode
  N13: R8.Pin_1, LED8.anode
  N14: R9.Pin_1, LED9.anode
  N15: R10.Pin_1, LED10.anode

notes:
  Router
  Display
  Controller
  Switches
  Lights
  GPS
  Heater
  +
  -
