# Fritzing sketch switch (saved by Fritzing 0.9.4)
circuit board: 8.33212cm x 4.59094cm
breadboards: 1

parts:
  Part2 = Arduino Nano 33 BLE Sense
  J3 = screw terminal, 2 pins
  J4 = screw terminal, 3 pins
  J5 = screw terminal, 2 pins
  J6 = screw terminal, 2 pins
  J7 = screw terminal, 3 pins
  J8 = screw terminal, 2 pins
  J9 = screw terminal, 3 pins

nets:
  N1: Part2.GND, Part2.A7, J3.pin2, J5.pin2, J6.pin2, J8.pin2
  N2: Part2.D2, J5.pin1
  N3: Part2.D3~, J4.pin3
  N4: Part2.D4, J4.pin1
  N5: Part2.D5~, J6.pin1
  N6: Part2.D6~, J7.pin3
  N7: Part2.D7, J7.pin1
  N8: Part2.D8, J8.pin1
  N9: Part2.D9~, J9.pin3
  N10: Part2.D10~, J9.pin1
  N11: Part2.VIN, J3.pin1
  N12: Part2.3V3, J4.pin2, J7.pin2, J9.pin2

notes:
  Dave Flanagan 2020
  +
  -
  B
  L
  R

custom parts:
  Arduino Nano 33 BLE Sense: The Nano 33 BLE Sense (without headers) is Arduino’s 3.3V AI enabled board in the smallest available form factor: 45x18mm! The Arduino Nano 33 BLE Sense is a completely new board on a well-known form factor. It comes with a series of embedded sensors: 9 axis inertial sensor: what makes this board ideal for wearable devices humidity, and temperature sensor: to get highly accurate measurements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
