# Fritzing sketch temperature (saved by Fritzing 0.9.4)
circuit board: 4.22187cm x 4.79744cm
breadboards: 1

parts:
  Part3 = Arduino Nano 33 BLE Sense
  J2 = screw terminal, 2 pins
  J3 = screw terminal, 4 pins
  R1 = Resistor [tolerance=±5% resistance=2.2k package=THT]
  R2 = Resistor [tolerance=±5% resistance=2.2k package=THT]

nets:
  N1: Part3.GND, J2.pin2, J3.pin4
  N2: Part3.D2, J3.pin3, R2.Pin_1
  N3: Part3.D3~, J3.pin2, R1.Pin_1
  N4: Part3.VIN, J2.pin1
  N5: Part3.3V3, J3.pin1, R1.Pin_0, R2.Pin_0

notes:
  VCC
  GND
  D3
  D2
  Dave Flanagan 2020

custom parts:
  Arduino Nano 33 BLE Sense: The Nano 33 BLE Sense (without headers) is Arduino’s 3.3V AI enabled board in the smallest available form factor: 45x18mm! The Arduino Nano 33 BLE Sense is a completely new board on a well-known form factor. It comes with a series of embedded sensors: 9 axis inertial sensor: what makes this board ideal for wearable devices humidity, and temperature sensor: to get highly accurate measurements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
